# Fritzing sketch ratpack_wifly (saved by Fritzing 0.7.10b)
breadboards: 1

parts:
  LED1 = LED - 5mm [color="Green (555nm)" package="5 mm [THT]"]
  S1 = Pushbutton [package=THT]
  R1 = Resistor [tolerance=±5% resistance=10k package=THT]
  Arduino1 = Arduino
  Bauteil1 = Arduino WiFly Shield

nets:
  GND: LED1.cathode, R1.Pin_0, Arduino1.GND, Bauteil1.GND
  N1: LED1.anode, Arduino1.D9, Bauteil1.D9
  +5V: S1.leg0, Arduino1.+5V, Bauteil1.5V
  N2: S1.leg1, R1.Pin_1, Arduino1.D2, Bauteil1.D2

notes:
  Would love to attache the Wifly shield to the arduino in this sketch - can't see how to do that.
