# Fritzing sketch ratpack_xbee_wifly (saved by Fritzing 0.7.12b)
breadboards: 1

parts:
  LED = LED - 5mm [color="Green (565nm)" package="5 mm [THT]"]
  R2_220_Ω = Resistor [tolerance=±5% resistance=220 package=THT]
  Switch = Pushbutton [package=THT]
  R1_10_kΩ = Resistor [tolerance=±5% resistance=10k package=THT]
  Arduino_Mini_Pro = Arduino Pro Mini 3.3V
  XBee_Wifly = XBee

nets:
  GND: LED.cathode, Arduino_Mini_Pro.GND, XBee_Wifly.GND
  N1: LED.anode, R2_220_Ω.Pin_1
  N2: R2_220_Ω.Pin_0, Arduino_Mini_Pro.D9
  VCC: Switch.leg0, R1_10_kΩ.Pin_0, Arduino_Mini_Pro.VCC, XBee_Wifly.VCC
  N3: Switch.leg1, R1_10_kΩ.Pin_1, Arduino_Mini_Pro.D2
  N4: Arduino_Mini_Pro.TXO, XBee_Wifly.pin3
  N5: Arduino_Mini_Pro.RXI, XBee_Wifly.pin2

notes:
  rat pack kit
  CC BY-SA 3.0 makingthingshappen.de
  github.com/5v3n/ratpack
